# Fritzing sketch birdhouse (saved by Fritzing 0.9.10b)
circuit board: 3cm x 5.64cm
circuit board: 5.51691cm x 3.08042cm
breadboards: 1

parts:
  Mod1 = Raspberry Pi 4B
  Q1 = Basic FET N-Channel [package="DPak [SMD]"]
  R1 = Resistor [tolerance=±5% power=0.25 resistance=15k package=THT]
  R2 = Resistor [tolerance=±5% resistance=3.3 package="2512 [SMD]"]
  R3 = Rotary Potentiometer (Small) [maximum_resistance=10kΩ knob_status=50% power=0.5W package=THT]
  LED1 = LED - 5mm [color="White (6500K)" current=0.030 package="5 mm [THT]"]
  LED2 = LED - 5mm [color="White (6500K)" current=0.030 package="5 mm [THT]"]
  LED3 = LED - 5mm [color="White (6500K)" current=0.030 package="5 mm [THT]"]
  LED4 = LED - 5mm [color="White (6500K)" current=0.030 package="5 mm [THT]"]
  LED5 = LED - 5mm [color="White (6500K)" current=0.030 package="5 mm [THT]"]
  LED6 = LED - 5mm [color="White (6500K)" current=0.030 package="5 mm [THT]"]
  LED7 = LED - 5mm [color="White (6500K)" current=0.030 package="5 mm [THT]"]
  LED8 = LED - 5mm [color="White (6500K)" current=0.030 package="5 mm [THT]"]
  LED9 = LED - 5mm [color="White (6500K)" current=0.030 package="5 mm [THT]"]
  LED10 = LED - 5mm [color="White (6500K)" current=0.030 package="5 mm [THT]"]
  JP1 = Header 2 [package=jst-2-pth]
  JP2 = Header 2 [package=jst-2-pth]

nets:
  N1: Mod1.5V, R2.Pin_0
  N2: Mod1.GND, Q1.source, R1.Pin_1
  N3: Mod1.GPIO4, Q1.Gate, R1.Pin_0
  N4: Q1.drain, LED1.cathode, LED2.cathode, LED3.cathode, LED4.cathode, LED5.cathode, LED6.cathode, LED7.cathode, LED8.cathode, LED9.cathode, LED10.cathode, JP2.2
  N5: R2.Pin_1, R3.wiper, JP1.2
  N6: R3.leg2, LED1.anode, LED2.anode, LED3.anode, LED4.anode, LED5.anode, LED6.anode, LED7.anode, LED8.anode, LED9.anode, LED10.anode, JP1.1, JP2.1

custom parts:
  Header 2: Header 2 Standard 2-pin 0.1 header. Private version, edited from Spakrfun library to get the 0.1in spacing and right graphics.
