# Fritzing sketch dust (saved by Fritzing 0.9.10b)
circuit board: 9cm x 7cm
breadboards: 1

parts:
  Part1 = ILI9488 TFT SPI 3.5 inch 480x320 w microSD [part_number=MSP3520]
  Part3 = Logic Level Converter
  Part4 = Logic Level Converter
  Part5 = Logic Level Converter
  Part7 = Arduino Nano (Rev3.0)
  JP1 = Header 6 [package=jst-6-pth]
  JP2 = Header 2 [package=jst-2-pth]
  JP3 = Header 1 [package=jst-1-pth]
  Part8 = LilyPad Slide Switch
  JP5 = Header 1 [package=jst-1-pth]
  J1 = Screw terminal - 2 pins [package=THT]

nets:
  VCC: Part1.VCC, Part3.LV, Part4.LV, Part5.LV, Part7.3V3
  GND: Part1.GND, Part3.GND, Part4.GND, Part5.GND, Part7.GND, JP2.2, J1.pin1
  N1: Part1.CS, Part4.TX_LV
  N2: Part1.RESET, Part4.RX_LV
  N3: Part1.DC/RS, Part4.RX2_LV
  N4: Part1.SDI(MOSI), Part4.TX2_LV
  N5: Part1.SCK, Part3.TX_LV
  N6: Part1.LED, Part3.RX_LV
  N7: Part1.T_CLK, Part3.RX2_LV
  N8: Part1.T_CS, Part3.TX2_LV
  N9: Part1.T_DIN, Part5.TX_LV
  N10: Part1.T_DO, Part5.RX_LV
  N11: Part1.T_IRQ, Part5.RX2_LV
  N12: Part3.TX_HV, Part7.D13/SCK
  N13: Part3.RX_HV, Part7.A0
  N14: Part3.HV, Part4.HV, Part5.HV, Part7.5V, JP2.1, Part8.ON, J1.pin2
  N15: Part3.RX2_HV, Part7.D3
  N16: Part3.TX2_HV, Part7.D2
  N17: Part4.TX_HV, Part7.A5
  N18: Part4.RX_HV, Part7.A4
  N19: Part4.RX2_HV, Part7.A3
  N20: Part4.TX2_HV, Part7.D11/MOSI
  N21: Part5.TX_HV, Part7.D5
  N22: Part5.RX_HV, Part7.D4
  N23: Part5.RX2_HV, Part7.D6
  N24: Part7.D7, JP1.4
  N25: Part7.D8, JP1.3
  N26: Part7.D9, JP1.2
  N27: Part7.D10, JP1.1
  N28: Part7.D12/MISO, JP3.1
  N29: Part7.A2, JP1.6
  N30: Part7.A1, JP1.5
  N31: Part8.OFF, JP5.1

custom parts:
  ILI9488 TFT SPI 3.5 inch 480x320 w microSD: 3.5" TFT touch display with SPI interface. 24bit RGB color, 480x320 pixels.
  Header 6: Header 6 Standard 6-pin 0.1 header. Private version, edited from Spakrfun library to get the 0.1in spacing and right graphics.
  Header 2: Header 2 Standard 2-pin 0.1 header. Private version, edited from Spakrfun library to get the 0.1in spacing and right graphics.
  Header 1: Header 1 Standard 1-pin 0.1 header. Private version, edited from Spakrfun library to get the 0.1in spacing and right graphics.
