# Fritzing sketch lpg_sensor (saved by Fritzing 0.9.6b)
circuit board: 8.47cm x 7.2cm
breadboards: 2

parts:
  Part1 = Gas Sensor Breakout Board
  VCC2 = Battery block 9V
  U2 = SWITCH-SPST-2 [package=switch-spst-vertical]
  Part3 = Arduino Nano (Rev3.0)
  Part4 = TFT 1.8 inch 160x128 w microSD [part_number=358]
  R1 = Resistor [tolerance=±5% resistance=10k package="0805 [SMD]"]
  U4 = I2C temperature and humidity sensor
  U3 = Voltage Regulator

nets:
  5V: Part1.A1, Part3.5V, Part4.LITE, Part4.+5V, U4.VDD
  N1: Part1.B1, Part3.A6, R1.Pin_0
  N2: Part1.H1, U3.OUT
  GND: Part1.GND, VCC2.-, Part3.GND, Part4.GND, R1.Pin_1, U4.GND, U3.GND
  N3: VCC2.+, U2.P
  N4: U2.O, Part3.VIN, U3.IN
  N5: Part3.D8, Part4.TFTDC
  N6: Part3.D9, Part4.RESET
  N7: Part3.D10, Part4.TFTCS
  N8: Part3.D11/MOSI, Part4.MOSI
  N9: Part3.A5, U4.SCL
  N10: Part3.A4, U4.SDA
  N11: Part3.D13/SCK, Part4.SCLK

custom parts:
  TFT 1.8 inch 160x128 w microSD: This lovely little display breakout is the best way to add a small, colorful and bright display to any project. Since the display uses 4-wire SPI to communicate and has its own pixel-addressable frame buffer, it can be used with every kind of microcontroller. Even a very small one with low memory and few pins available! The 1.8" display has 128x160 color pixels.
  I2C temperature and humidity sensor: DHT20 Temperature and Humidity Sensor
  Voltage Regulator: DC-DC power, 5V. CUI Inc VXO7805-500-M DC-DC power supply, 6.5-36V input
