# Fritzing sketch touchscreen (saved by Fritzing 0.9.6b)
circuit board: 10cm x 6cm
breadboards: 1

parts:
  Part1 = ILI9488 TFT SPI 3.5 inch 480x320 w microSD [part_number=MSP3520]
  Part3 = Logic Level Converter
  Part4 = Logic Level Converter
  Part5 = Logic Level Converter
  Part6 = Arduino Uno (Rev3) - ICSP

nets:
  VCC: Part1.VCC, Part3.LV, Part4.LV, Part5.LV, Part6.3V3
  GND: Part1.GND, Part3.GND, Part4.GND, Part5.GND, Part6.GND
  N1: Part1.CS, Part4.TX_LV
  N2: Part1.RESET, Part4.RX_LV
  N3: Part1.DC/RS, Part4.RX2_LV
  N4: Part1.SDI(MOSI), Part4.TX2_LV
  N5: Part1.SCK, Part3.TX_LV
  N6: Part1.LED, Part3.RX_LV
  N7: Part1.T_CLK, Part3.RX2_LV
  N8: Part1.T_CS, Part3.TX2_LV
  N9: Part1.T_DIN, Part5.TX_LV
  N10: Part1.T_DO, Part5.RX_LV
  N11: Part1.T_IRQ, Part5.RX2_LV
  N12: Part3.TX_HV, Part6.D13/SCK
  N13: Part3.RX_HV, Part6.A0
  N14: Part3.HV, Part4.HV, Part5.HV, Part6.5V
  N15: Part3.RX2_HV, Part6.D3_PWM
  N16: Part3.TX2_HV, Part6.D2
  N17: Part4.TX_HV, Part6.A5/SCL
  N18: Part4.RX_HV, Part6.A4/SDA
  N19: Part4.RX2_HV, Part6.A3
  N20: Part4.TX2_HV, Part6.D11_PWM/MOSI
  N21: Part5.TX_HV, Part6.D5_PWM
  N22: Part5.RX_HV, Part6.D4
  N23: Part5.RX2_HV, Part6.D6_PWM

custom parts:
  ILI9488 TFT SPI 3.5 inch 480x320 w microSD: 3.5" TFT touch display with SPI interface. 24bit RGB color, 480x320 pixels.
